// Logisim project stopwatch.circ as structural Verilog: 3 circuits, main circuit main
module BCD_0to9 (
  input  CLR,
  input  EN,
  input  CLK,
  output CARRY,
  output [3:0] Q
);

  wire counter_1_carry;

  Counter #(.max('h9), .width(4)) counter_1 (
    .clr(CLR), .load(EN), .up(1'b1), .clk(CLK), .carry(counter_1_carry), .Q(Q));  // open: count, D
  not not_1 (CARRY, counter_1_carry);
endmodule

module BCD_0to5 (
  input  CLR,
  input  EN,
  input  CLK,
  output CARRY,
  output [3:0] Q
);

  wire counter_1_carry;

  Counter #(.max('h5), .width(4)) counter_1 (
    .clr(CLR), .load(EN), .up(1'b1), .clk(CLK), .carry(counter_1_carry), .Q(Q));  // open: count, D
  not not_1 (CARRY, counter_1_carry);
endmodule

module main (
);

  wire CLK_1Hz_out, CLR, EN, EN_FF_qn, HR_ONES_carry, MIN_ONES_carry, MIN_TENS_carry, SEC_ONES_carry,
       SEC_TENS_carry, START_out, STOP_out;
  wire [3:0] bcd_to_7_segment_decoder_1_p1, bcd_to_7_segment_decoder_2_p1, bcd_to_7_segment_decoder_3_p1,
       bcd_to_7_segment_decoder_4_p1, SEC_ONES_q, SEC_TENS_q;

  Button STOP (.out(STOP_out));
  Button START (.out(START_out));
  Button RESET (.out(CLR));
  Clock #(.highDuration(500), .lowDuration(500)) CLK_1Hz (.out(CLK_1Hz_out));
  D_Flip_Flop EN_FF (.D(EN_FF_qn), .clk(STOP_out), .Q(EN), .Qn(EN_FF_qn), .preset(CLR), .reset(START_out));
  BCD_0to9 SEC_ONES (.CLR(CLR), .EN(EN), .CLK(CLK_1Hz_out), .CARRY(SEC_ONES_carry), .Q(SEC_ONES_q));
  BCD_0to5 SEC_TENS (.CLR(CLR), .EN(EN), .CLK(SEC_ONES_carry), .CARRY(SEC_TENS_carry), .Q(SEC_TENS_q));
  _7_Segment_Display HH_tens ();  // open: g, f, a, b, e, d, c, dp
  // BCD_to_7_Segment_decoder bcd_to_7_segment_decoder_1: pin names not known; wires that end beside it: bcd_to_7_segment_decoder_1_p1
  _7_Segment_Display HH_ones ();  // open: g, f, a, b, e, d, c, dp
  _7_Segment_Display MM_tens ();  // open: g, f, a, b, e, d, c, dp
  // BCD_to_7_Segment_decoder bcd_to_7_segment_decoder_2: pin names not known; wires that end beside it: bcd_to_7_segment_decoder_2_p1
  // BCD_to_7_Segment_decoder bcd_to_7_segment_decoder_3: pin names not known; wires that end beside it: bcd_to_7_segment_decoder_3_p1
  _7_Segment_Display MM_ones ();  // open: g, f, a, b, e, d, c, dp
  // BCD_to_7_Segment_decoder bcd_to_7_segment_decoder_4: pin names not known; wires that end beside it: bcd_to_7_segment_decoder_4_p1
  _7_Segment_Display SS_tens ();  // open: g, f, a, b, e, d, c, dp
  // BCD_to_7_Segment_decoder bcd_to_7_segment_decoder_5: pin names not known; wires that end beside it: SEC_TENS_q
  BCD_0to9 MIN_ONES (
    .CLR(CLR), .EN(EN), .CLK(SEC_TENS_carry), .CARRY(MIN_ONES_carry), .Q(bcd_to_7_segment_decoder_4_p1));
  _7_Segment_Display SS_ones ();  // open: g, f, a, b, e, d, c, dp
  // BCD_to_7_Segment_decoder bcd_to_7_segment_decoder_6: pin names not known; wires that end beside it: SEC_ONES_q
  BCD_0to5 MIN_TENS (
    .CLR(CLR), .EN(EN), .CLK(MIN_ONES_carry), .CARRY(MIN_TENS_carry), .Q(bcd_to_7_segment_decoder_3_p1));
  BCD_0to9 HR_ONES (.CLR(CLR), .EN(EN), .CLK(MIN_TENS_carry), .CARRY(HR_ONES_carry), .Q(bcd_to_7_segment_decoder_2_p1));
  BCD_0to9 HR_TENS (.CLR(CLR), .EN(EN), .CLK(HR_ONES_carry), .Q(bcd_to_7_segment_decoder_1_p1));  // open: CARRY
endmodule
